// Logisim project Alarm_Clock_104756611.circ as structural Verilog: 1 circuit, main circuit main
module main (
  input  in_1,
  input  in_2
);

  wire and_1_out, and_2_out, and_3_out, and_4_out, and_5_out, and_6_out, and_7_out, and_8_out, and_9_out,
       and_10_out, and_11_out, and_12_out, and_13_out, and_14_out, and_15_out, and_16_out, and_17_out,
       and_18_out, and_19_out, and_20_out, and_21_out, button_1_out, button_2_out, button_3_out,
       button_4_out, button_5_out, button_6_out, clock_1_out, d_ff_1_q, d_ff_1_qn, j_k_ff_1_q, j_k_ff_2_q,
       j_k_ff_3_q, j_k_ff_4_q, j_k_ff_5_q, j_k_ff_6_q, j_k_ff_6_qn, not_1_out, not_2_out, or_1_out, or_2_out,
       or_3_out, or_4_out, or_5_out, or_6_out, or_7_out, or_8_out, or_9_out, or_10_out, xnor_1_out,
       xnor_2_out, xnor_3_out, xnor_4_out, xnor_5_out, xnor_6_out, xnor_7_out, xnor_8_out, xnor_9_out,
       xnor_10_out, xnor_11_out, xnor_12_out, xnor_13_out;
  wire [0:0] d_ff_2_q, j_k_ff_7_q;
  wire [2:0] d_ff_9_q, j_k_ff_14_q;
  wire [3:0] d_ff_6_q, d_ff_13_q, j_k_ff_11_q, j_k_ff_18_q;

  J_K_Flip_Flop j_k_ff_1 (
    .J(and_1_out), .K(and_1_out), .clk(or_5_out), .Q(j_k_ff_1_q), .reset(or_6_out));  // open: Qn, preset
  and and_1 (and_1_out, and_2_out, j_k_ff_2_q);
  J_K_Flip_Flop j_k_ff_2 (
    .J(and_2_out), .K(and_2_out), .clk(or_5_out), .Q(j_k_ff_2_q), .reset(or_6_out));  // open: Qn, preset
  and and_2 (and_2_out, and_3_out, j_k_ff_3_q);
  J_K_Flip_Flop j_k_ff_3 (
    .J(and_3_out), .K(and_3_out), .clk(or_5_out), .Q(j_k_ff_3_q), .reset(or_6_out));  // open: Qn, preset
  and and_3 (and_3_out, j_k_ff_5_q, j_k_ff_4_q);
  J_K_Flip_Flop j_k_ff_4 (
    .J(j_k_ff_5_q), .K(j_k_ff_5_q), .clk(or_5_out), .Q(j_k_ff_4_q), .reset(or_6_out));  // open: Qn, preset
  J_K_Flip_Flop j_k_ff_5 (.J(1'b1), .K(1'b1), .clk(or_5_out), .Q(j_k_ff_5_q), .reset(or_6_out));  // open: Qn, preset
  and and_4 (and_4_out, j_k_ff_2_q, j_k_ff_1_q);
  D_Flip_Flop d_ff_1 (
    .D(j_k_ff_6_q), .clk(button_1_out), .Q(d_ff_1_q), .Qn(d_ff_1_qn), .reset(button_2_out));  // open: preset
  J_K_Flip_Flop j_k_ff_6 (
    .J(1'b1), .K(1'b1), .clk(and_5_out), .Q(j_k_ff_6_q), .Qn(j_k_ff_6_qn), .reset(or_6_out));  // open: preset
  and and_5 (and_5_out, j_k_ff_11_q[1], j_k_ff_7_q[0]);
  xnor xnor_1 (xnor_1_out, d_ff_1_q, j_k_ff_6_q);
  D_Flip_Flop d_ff_2 (
    .D(j_k_ff_7_q[0]), .clk(button_1_out), .Q(d_ff_2_q[0]), .reset(button_2_out));  // open: Qn, preset
  J_K_Flip_Flop #(.trigger("falling")) j_k_ff_7 (
    .J(1'b1), .K(1'b1), .clk(and_8_out), .Q(j_k_ff_7_q[0]), .reset(or_1_out));  // open: Qn, preset
  or or_1 (or_1_out, or_6_out, and_7_out);
  xnor xnor_2 (xnor_2_out, d_ff_2_q[0], j_k_ff_7_q[0]);
  and and_6 (and_6_out, xnor_1_out, xnor_2_out);
  and and_7 (and_7_out, j_k_ff_7_q[0], j_k_ff_11_q[1], j_k_ff_11_q[0]);
  and and_8 (and_8_out, j_k_ff_11_q[3], j_k_ff_11_q[1]);
  D_Flip_Flop d_ff_3 (
    .D(j_k_ff_11_q[3]), .clk(button_1_out), .Q(d_ff_6_q[3]), .reset(button_2_out));  // open: Qn, preset
  J_K_Flip_Flop j_k_ff_8 (
    .J(and_9_out), .K(and_9_out), .clk(or_5_out), .Q(j_k_ff_11_q[3]), .reset(or_3_out));  // open: Qn, preset
  xnor xnor_3 (xnor_3_out, d_ff_6_q[3], j_k_ff_11_q[3]);
  and and_9 (and_9_out, and_10_out, j_k_ff_11_q[2]);
  D_Flip_Flop d_ff_4 (
    .D(j_k_ff_11_q[2]), .clk(button_1_out), .Q(d_ff_6_q[2]), .reset(button_2_out));  // open: Qn, preset
  J_K_Flip_Flop j_k_ff_9 (
    .J(and_10_out), .K(and_10_out), .clk(or_5_out), .Q(j_k_ff_11_q[2]), .reset(or_3_out));  // open: Qn, preset
  xnor xnor_4 (xnor_4_out, d_ff_6_q[2], j_k_ff_11_q[2]);
  and and_10 (and_10_out, j_k_ff_11_q[0], j_k_ff_11_q[1]);
  or or_2 (or_2_out, and_8_out, and_7_out);
  D_Flip_Flop d_ff_5 (
    .D(j_k_ff_11_q[1]), .clk(button_1_out), .Q(d_ff_6_q[1]), .reset(button_2_out));  // open: Qn, preset
  J_K_Flip_Flop j_k_ff_10 (
    .J(j_k_ff_11_q[0]), .K(j_k_ff_11_q[0]), .clk(or_5_out), .Q(j_k_ff_11_q[1]), .reset(or_3_out));  // open: Qn, preset
  or or_3 (or_3_out, or_2_out, or_6_out);
  xnor xnor_5 (xnor_5_out, d_ff_6_q[1], j_k_ff_11_q[1]);
  D_Flip_Flop d_ff_6 (
    .D(j_k_ff_11_q[0]), .clk(button_1_out), .Q(d_ff_6_q[0]), .reset(button_2_out));  // open: Qn, preset
  J_K_Flip_Flop j_k_ff_11 (
    .J(1'b1), .K(1'b1), .clk(or_5_out), .Q(j_k_ff_11_q[0]), .preset(and_7_out), .reset(or_4_out));  // open: Qn
  or or_4 (or_4_out, and_8_out, or_6_out);
  xnor xnor_6 (xnor_6_out, d_ff_6_q[0], j_k_ff_11_q[0]);
  and and_11 (and_11_out, xnor_3_out, xnor_4_out, xnor_5_out, xnor_6_out);
  or or_5 (or_5_out, button_3_out, and_16_out);
  Button button_1 (.out(button_1_out));
  Button button_2 (.out(button_2_out));
  Button button_3 (.out(button_3_out));
  LED led_1 (.in(d_ff_1_qn));
  LED led_2 (.in(j_k_ff_6_qn));
  LED led_3 (.in(d_ff_1_q));
  Hex_Digit_Display hex_digit_display_1 (.value({3'b000, d_ff_2_q[0]}));  // open: dp
  LED led_4 (.in(j_k_ff_6_q));
  Hex_Digit_Display hex_digit_display_2 (.value({3'b000, j_k_ff_7_q[0]}));  // open: dp
  and and_12 (and_12_out, and_11_out, and_6_out, and_17_out, and_14_out);
  LED led_5 (.in(and_12_out));
  LED led_6 (.in(and_12_out));
  Hex_Digit_Display hex_digit_display_3 (.value(d_ff_6_q));  // open: dp
  Hex_Digit_Display hex_digit_display_4 (.value(j_k_ff_11_q));  // open: dp
  LED led_7 (.in(and_12_out));
  LED led_8 (.in(and_12_out));
  Hex_Digit_Display hex_digit_display_5 (.value({1'b0, d_ff_9_q}));  // open: dp
  Hex_Digit_Display hex_digit_display_6 (.value({1'b0, j_k_ff_14_q}));  // open: dp
  Hex_Digit_Display hex_digit_display_7 (.value(d_ff_13_q));  // open: dp
  Hex_Digit_Display hex_digit_display_8 (.value(j_k_ff_18_q));  // open: dp
  Button button_4 (.out(button_4_out));
  Button button_5 (.out(button_5_out));
  Button button_6 (.out(button_6_out));
  not not_1 (not_1_out, in_1);
  not not_2 (not_2_out, in_2);
  and and_13 (and_13_out, not_1_out, not_2_out);
  or or_6 (or_6_out, button_6_out, and_4_out);
  and and_14 (and_14_out, xnor_9_out, xnor_8_out, xnor_7_out);
  D_Flip_Flop d_ff_7 (
    .D(j_k_ff_14_q[2]), .clk(button_1_out), .Q(d_ff_9_q[2]), .reset(button_2_out));  // open: Qn, preset
  J_K_Flip_Flop j_k_ff_12 (
    .J(and_15_out), .K(and_15_out), .clk(or_8_out), .Q(j_k_ff_14_q[2]), .reset(or_7_out));  // open: Qn, preset
  xnor xnor_7 (xnor_7_out, d_ff_9_q[2], j_k_ff_14_q[2]);
  and and_15 (and_15_out, j_k_ff_14_q[0], j_k_ff_14_q[1]);
  D_Flip_Flop d_ff_8 (
    .D(j_k_ff_14_q[1]), .clk(button_1_out), .Q(d_ff_9_q[1]), .reset(button_2_out));  // open: Qn, preset
  J_K_Flip_Flop j_k_ff_13 (
    .J(j_k_ff_14_q[0]), .K(j_k_ff_14_q[0]), .clk(or_8_out), .Q(j_k_ff_14_q[1]), .reset(or_7_out));  // open: Qn, preset
  xnor xnor_8 (xnor_8_out, d_ff_9_q[1], j_k_ff_14_q[1]);
  and and_16 (and_16_out, j_k_ff_14_q[1], j_k_ff_14_q[2]);
  D_Flip_Flop d_ff_9 (
    .D(j_k_ff_14_q[0]), .clk(button_1_out), .Q(d_ff_9_q[0]), .reset(button_2_out));  // open: Qn, preset
  J_K_Flip_Flop j_k_ff_14 (
    .J(1'b1), .K(1'b1), .clk(or_8_out), .Q(j_k_ff_14_q[0]), .reset(or_7_out));  // open: Qn, preset
  xnor xnor_9 (xnor_9_out, d_ff_9_q[0], j_k_ff_14_q[0]);
  or or_7 (or_7_out, and_16_out, or_6_out);
  or or_8 (or_8_out, button_4_out, and_20_out);
  and and_17 (and_17_out, xnor_13_out, xnor_12_out, xnor_11_out, xnor_10_out);
  J_K_Flip_Flop j_k_ff_15 (
    .J(and_18_out), .K(and_18_out), .clk(or_10_out), .Q(j_k_ff_18_q[3]), .reset(or_9_out));  // open: Qn, preset
  D_Flip_Flop d_ff_10 (
    .D(j_k_ff_18_q[3]), .clk(button_1_out), .Q(d_ff_13_q[3]), .reset(button_2_out));  // open: Qn, preset
  xnor xnor_10 (xnor_10_out, d_ff_13_q[3], j_k_ff_18_q[3]);
  and and_18 (and_18_out, and_19_out, j_k_ff_18_q[2]);
  D_Flip_Flop d_ff_11 (
    .D(j_k_ff_18_q[2]), .clk(button_1_out), .Q(d_ff_13_q[2]), .reset(button_2_out));  // open: Qn, preset
  J_K_Flip_Flop j_k_ff_16 (
    .J(and_19_out), .K(and_19_out), .clk(or_10_out), .Q(j_k_ff_18_q[2]), .reset(or_9_out));  // open: Qn, preset
  xnor xnor_11 (xnor_11_out, d_ff_13_q[2], j_k_ff_18_q[2]);
  and and_19 (and_19_out, j_k_ff_18_q[0], j_k_ff_18_q[1]);
  D_Flip_Flop d_ff_12 (
    .D(j_k_ff_18_q[1]), .clk(button_1_out), .Q(d_ff_13_q[1]), .reset(button_2_out));  // open: Qn, preset
  J_K_Flip_Flop j_k_ff_17 (
    .J(j_k_ff_18_q[0]), .K(j_k_ff_18_q[0]), .clk(or_10_out), .Q(j_k_ff_18_q[1]), .reset(or_9_out));  // open: Qn, preset
  xnor xnor_12 (xnor_12_out, d_ff_13_q[1], j_k_ff_18_q[1]);
  and and_20 (and_20_out, j_k_ff_18_q[1], j_k_ff_18_q[3]);
  D_Flip_Flop d_ff_13 (
    .D(j_k_ff_18_q[0]), .clk(button_1_out), .Q(d_ff_13_q[0]), .reset(button_2_out));  // open: Qn, preset
  J_K_Flip_Flop j_k_ff_18 (
    .J(1'b1), .K(1'b1), .clk(or_10_out), .Q(j_k_ff_18_q[0]), .reset(or_9_out));  // open: Qn, preset
  xnor xnor_13 (xnor_13_out, d_ff_13_q[0], j_k_ff_18_q[0]);
  or or_9 (or_9_out, and_20_out, or_6_out);
  or or_10 (or_10_out, button_5_out, and_21_out);
  and and_21 (and_21_out, clock_1_out, and_13_out);
  Clock clock_1 (.out(clock_1_out));

  // Notes on the sheet:
  //   24 Hour Reset Counter
  //   Reset Signal After 24Hrs
  //   RESET
  //   CLK
  //   Hex Display Display 12
  //   User Reset Signal
  //   Previous Counter Increment Signal
  //   HEX Display
  //   User Reset Signal
  //   Q0
  //   2 HEX Displays Display 13
  //   2 HEX Displays Display 13
  //   HEX Display
  //   Counter Reaches 10
  //   Q3
  //   Q3
  //   Q2
  //   Counter Reaches 10
  //   2 HEX Displays Display 13
  //   Q1
  //   Q1
  //   Q1
  //   Q1
  //   User Reset Signal
  //   Power
  //   Counter Reaches 10
  //   Q0
  //   Q0
  //   User Reset Signal
  //   2 HEX Displays Display 13
  //   Increment Signal From Previous Counter
  //   User Increment Signal
  //   AM
  //   PM
  //   Set Alarm 
  //   Reset Alarm
  //   Increment Hours
  //   AM
  //   PM
  //   Alarm Triggered
  //   Alarm
  //   Clock
  //   Increment Minutes (10s)
  //   Increment Minutes (Units)
  //   Edit Alarm Time
  //   Edit Clock Time
  //   Reset Clock
  //   User Reset Signal
  //   Reset Signal After 24Hrs
  //   HEX Display
  //   Q2
  //   Q2
  //   Q1
  //   Q1
  //   Counter Reaches Value 6
  //   Increment Signal for Next Counter
  //   Power
  //   Q0
  //   Reset Signal at 6
  //   CLK
  //   RESET
  //   User Reset Signal
  //   User Increment Minute Signal
  //   Previous Counter Increment Signal
  //   HEX Display
  //   Q3
  //   Q3
  //   Q2
  //   Q1
  //   Q1
  //   Counter Reaches Value 10
  //   Increment Signal for Next Counter
  //   Power
  //   Q0
  //   Reset Signal at 10
  //   CLK
  //   RESET
  //   User Reset Signal
  //   User Increment Signal
  //   Edit Time/ Alarm Signal
  //   Edit Time/ Alarm Signal
endmodule
